// Logisim project demo3_0913.circ as structural Verilog: 4 circuits, main circuit main
module main (
  input  in_1,
  input  \_2_震荡 ,
  input  \使能 ,
  input  [1:0] \选择 ,
  output out_5,
  output out_6
);

  wire buffer_1_out, not_1_out;

  buf buffer_1 (buffer_1_out, in_1);
  not not_1 (not_1_out, in_1);
  nand nand_1 (out_6, \_2_震荡 , out_6);
  and and_1 (out_5, buffer_1_out, ~not_1_out);  // AND_Gate
  Counter counter_1 (.clk(out_5));  // open: load, D, count, Q, carry, clr
  Pull_Resistor pull_resistor_1 ();  // open: node
  Multiplexer #(.select(2), .width(2)) multiplexer_1 (.sel(\选择 ), .en(\使能 ));  // open: in0, in1, in2, in3, out
  Demultiplexer #(.select(4), .width(2)) demultiplexer_1 ();  // open: out0, out1, out2, out3, out4, out5, out6, out7, out8, out9, out10, out11, out12, out13, out14, out15, in, sel, en

  // Notes on the sheet:
  //   险象
  //   1、竞争
  //   单步调试
  //   消除竞争
  //   消除方法： 输入改为0， 修改为实时调试
  //   不要用输入引脚当常量
  //   用电源或者接地
  //   不要当做if-else的实现组件
  //   复杂，时间延迟高
endmodule

// 编码器
module \第三次实验  (
  input  In1,
  input  In2,
  input  In3,
  input  In4,
  input  In5,
  output Out1,
  output Out2,
  output Out3,
  output Out4,
  output Out5
);

  or or_1 (Out1, In1, In2, In3, In4, In5);
  or or_2 (Out2, In2, In3, In4, In5);
  or or_3 (Out3, In3, In4, In5);
  or or_4 (Out4, In4, In5);

  assign Out5 = In5;

  // Notes on the sheet:
  //   入门实验1、LED计数电路
  //   优先
endmodule

// LED计数
module \LED电路测试  (
);

  wire _1_out, _2_out, _3_out, _4_out, _5_out, \第三次实验_1_out1 , \第三次实验_1_out2 , \第三次实验_1_out3 ,
       \第三次实验_1_out4 , \第三次实验_1_out5 ;
  wire [2:0] \n5输入按键编码器_1_out1 ;

  Button _1 (.out(_1_out));
  Button _2 (.out(_2_out));
  Button _3 (.out(_3_out));
  Button _4 (.out(_4_out));
  Button _5 (.out(_5_out));
  \第三次实验  \u_第三次实验_1  (
    .In1(_1_out), .In2(_2_out), .In3(_3_out), .In4(_4_out), .In5(_5_out), .Out1(\第三次实验_1_out1 ),
    .Out2(\第三次实验_1_out2 ), .Out3(\第三次实验_1_out3 ), .Out4(\第三次实验_1_out4 ), .Out5(\第三次实验_1_out5 ));
  \_5输入按键编码器  \u_5输入按键编码器_1  (
    .In1(_1_out), .In2(_2_out), .In3(_3_out), .In4(_4_out), .In5(_5_out), .Out1(\n5输入按键编码器_1_out1 [0]),
    .Out2(\n5输入按键编码器_1_out1 [1]), .Out3(\n5输入按键编码器_1_out1 [2]));
  LED led_1 (.in(\第三次实验_1_out1 ));
  LED led_2 (.in(\第三次实验_1_out2 ));
  // Probe on \n5输入按键编码器_1_out1 
  LED led_3 (.in(\第三次实验_1_out3 ));
  LED led_4 (.in(\第三次实验_1_out4 ));
  LED led_5 (.in(\第三次实验_1_out5 ));
  Hex_Digit_Display hex_digit_display_1 (.value({1'b0, \n5输入按键编码器_1_out1 }));  // open: dp
endmodule

// 编码器
module \_5输入按键编码器  (
  input  In1,
  input  In2,
  input  In3,
  input  In4,
  input  In5,
  output Out1,
  output Out2,
  output Out3
);

  wire and_1_out, and_2_out, and_3_out, and_4_out, not_1_out, not_2_out, not_3_out, not_4_out, not_5_out,
       not_6_out, not_7_out;

  not not_1 (not_1_out, In4);
  not not_2 (not_2_out, In2);
  not not_3 (not_3_out, In4);
  not not_4 (not_4_out, In4);
  not not_5 (not_5_out, In5);
  not not_6 (not_6_out, In4);
  not not_7 (not_7_out, In5);
  or or_1 (Out3, In5, In4);
  and and_1 (and_1_out, In3, not_1_out);
  and and_2 (and_2_out, In1, not_2_out, not_3_out);
  and and_3 (and_3_out, In3, not_4_out, not_5_out);
  and and_4 (and_4_out, In2, not_6_out, not_7_out);
  or or_2 (Out1, In5, and_1_out, and_2_out);
  or or_3 (Out2, and_3_out, and_4_out);
endmodule
