// Logisim project demo1.circ as structural Verilog: 2 circuits, main circuit main
module main (
  input  [1:0] \可相互转换 ,
  input  [1:0] \输出引脚 ,
  input  in_3,
  input  in_4,
  input  in_5,
  input  in_6,
  input  [22:0] in_7,
  input  [22:0] in_8,
  input  in_9,
  input  in_10,
  input  in_11,
  input  s,
  output out_13,
  output [22:0] z
);

  wire button_1_out, clock_1_out, d_ff_1_q, d_ff_2_q, d_ff_3_q, undriven;
  wire [22:0] and_2_out, or_1_out;

  Clock clock_1 (.out(clock_1_out));
  _7_Segment_Display u_7_segment_display_1 (
    .g(in_5), .f(in_3), .a(in_4), .e(in_9), .d(in_11), .c(in_10), .dp(in_6));  // open: b
  D_Flip_Flop d_ff_1 (
    .clk(clock_1_out), .D(d_ff_3_q), .Q(d_ff_1_q), .en(undriven), .reset(undriven));  // open: Qn, preset
  D_Flip_Flop d_ff_2 (.clk(clock_1_out), .D(d_ff_1_q), .Q(d_ff_2_q));  // open: Qn, preset, en, reset
  D_Flip_Flop d_ff_3 (.clk(clock_1_out), .D(d_ff_2_q), .Q(d_ff_3_q));  // open: Qn, preset, en, reset
  Button button_1 (.out(button_1_out));
  // AND_Gate and_1 is placed but not wired
  LED led_1 (.in(button_1_out));
  assign and_2_out = in_7 & in_8;  // AND_Gate and_2, 23 bits wide
  assign or_1_out = in_7 | in_8;  // OR_Gate or_1, 23 bits wide
  // Probe on and_2_out
  Multiplexer #(.width(23), .enable("false")) multiplexer_1 (.in0(and_2_out), .in1(or_1_out), .out(z), .sel(s));
  // Pins of 1 and 2 bits meet at \可相互转换 

  assign out_13 = \可相互转换 [0];

  // Notes on the sheet:
  //   输入引脚
  //   ctrl + D; alt + num; up and down
  //   delete
  //    counter
  //   johnson
  //   小键盘
  //   更改位宽
  //   探测器(probe)
  //   相互转换的不一样
  //   全选再alt
endmodule

module not_main (
);

  main main_1 ();  // open: in_3, in_4, in_5, in_6, in_7, in_8, in_9, in_10, in_11, s, out_13, z, 可相互转换, 输出引脚
endmodule
