// Logisim project demo2.circ as structural Verilog: 3 circuits, main circuit main
module main (
  input  x,
  input  y,
  output o
);

  wire and_1_out, or_1_out;

  and and_1 (and_1_out, x, y);
  or or_1 (or_1_out, x, y);
  and and_2 (o, and_1_out, or_1_out);
endmodule

module empty (
  input  x,
  input  y,
  input  Cin,
  output Sum,
  output Cout
);

  wire and_1_out, and_2_out, and_3_out;

  xor odd_parity_1 (Sum, x, y, Cin);
  and and_1 (and_1_out, x, y);
  and and_2 (and_2_out, x, Cin);
  and and_3 (and_3_out, y, Cin);
  or or_1 (Cout, and_1_out, and_2_out, and_3_out);
endmodule

module label (
);


  // Notes on the sheet:
  //   不同真值表得出的不一样，险象与延迟
  //   化简电路，得出表达式，一步一步模拟，全部控制器清零，自动生成电路（有限制
endmodule
